# Fritzing sketch SparkFun.Bonnet (saved by Fritzing 0.9.3b)
breadboards: 1

parts:
  Raspberry_Pi_Zero1 = Raspberry Pi Zero  # not connected
  IC1 = MCP3008 8-channel 10-bit ADC [part_number=MCP3008]
  Part2 = Soil Moisture Sensor
  KY-1 = Keyes Relay [package=THT]
  Part3 = Lilypad Power Supply
  J2 = Screw terminal - 2 pins [package=THT]
  J3 = Screw terminal - 2 pins [package=THT]
  U1 = LIPO-2000mAh [package=lipo-2000]  # not connected
  JP3 = Header 3 [package=screwterminal-3.5mm-3_lock.007s]
  JP1 = Header 3 [package=screwterminal-3.5mm-3_lock.007s]
  D1 = Rectifier Diode [part_number=1N4001 package="Melf DO-213 AB [SMD]"]
  Part5 = PowerBoost 500 Charger

nets:
  N1: IC1.no_name_yet#1, Part2.SIG, JP3.2
  N2: IC1.no_name_yet#9, IC1.no_name_yet#14, KY-1.ground, J2.pin2, J3.pin1
  N3: IC1.no_name_yet#15, IC1.no_name_yet#16, Part2.VCC, KY-1.signal, J3.pin2, JP3.1
  GND: Part2.GND, Part3.GND, JP1.1, Part5.GND
  N4: KY-1.NO, D1.anode
  N5: Part3.+, J2.pin1, JP1.2, Part5.USB

notes:
  5v Water pump
  https://www.allelectronics.com/item/pmp-20/mini-water-pump/1.html
  + -
  5v Power Supply.
  A 5v AC adaptor works too.
  Raspberry Pi Zero under the Adafruit Bonnet. Powered by the Bonnet.
  Notice the PowerBoost (500 or 1000) and the LiPo battery.
  The power supply is powering the booster, that in turn powers the pump, through its LiPo battery.
  The reason for that is that it is difficult (if even possible) to power the Raspberry Pi and the Pump from the same 5v source. When the pump starts, this generates a voltage drop that makes the Raspberry Pi reboot...
  In this configuration, the booster and its LiPo battery are acting as a buffer on the power supply line.
  The rectifier diode is here for similar reasons.
  Connections to the outside world
  Rectifier Diode on the way out to the pump.

custom parts:
  Keyes Relay: The Keyes 5V relay module is suitable for SCM development, home appliance control. It uses a 5V~12V TIL control signal which can control DC / AC signal.
